# Fritzing sketch Arduino Speed Time Track Fritzing (saved by Fritzing 0.9.3b)
breadboards: 1

parts:
  Part1 = Arduino Uno (Rev3)
  R1 = Resistor [tolerance=±5% resistance=10k package=THT]
  LDR1 = Photocell (LDR) [package=THT]
  LDR2 = Photocell (LDR) [package=THT]
  R2 = Resistor [tolerance=±5% resistance=10k package=THT]
  R3 = Resistor [tolerance=±5% resistance=10k package=THT]
  R4 = Resistor [tolerance=±5% resistance=10k package=THT]
  LDR3 = Photocell (LDR) [package=THT]
  LDR4 = Photocell (LDR) [package=THT]

nets:
  N1: Part1.A0, R1.Pin_1, LDR1.pin_0
  N2: Part1.A1, LDR2.pin_0, R2.Pin_1
  N3: Part1.A2, R3.Pin_1, LDR3.pin_0
  N4: Part1.A3, R4.Pin_1, LDR4.pin_0
  N5: Part1.5V, LDR1.pin_1, LDR2.pin_1, LDR3.pin_1, LDR4.pin_1
  N6: Part1.GND, R1.Pin_0, R2.Pin_0, R3.Pin_0, R4.Pin_0

notes:
  Sensor 1
  Sensor 2
  Sensor 3
  Sensor 4
